# Fritzing sketch 11 (saved by Fritzing 0.9.3b)
breadboards: 1

parts:
  Seven_Segment_Display = Header 12 [package=1x12_machine-pin-header_lock.004]

nets:
  Arduino GPIO6: Seven_Segment_Display.1
  Arduino GPIO7: Seven_Segment_Display.2
  Arduino GPIO8: Seven_Segment_Display.3
  Arduino GPIO9: Seven_Segment_Display.4
  Arduino GPIO10: Seven_Segment_Display.5
  Arduino GPIO2: Seven_Segment_Display.6
  Arduino GPIO11: Seven_Segment_Display.7
  Arduino GPIO3: Seven_Segment_Display.8
  Arduino GPIO4: Seven_Segment_Display.9
  Arduino GPIO12: Seven_Segment_Display.10
  Arduino GPIO13: Seven_Segment_Display.11
  Arduino GPIO5: Seven_Segment_Display.12

notes:
  D1
  D2
  D3
  D4
  DP
  A
  B
  D
  C
  E
  F
  G
